// Logisim project Lab_6_cybernetica.circ as structural Verilog: 7 circuits, main circuit SR триггер
module Lab_6 (
  input  \SR_триггер ,
  input  in_2,
  input  in_3,
  input  in_4,
  input  in_5,
  input  in_6,
  input  in_7,
  input  in_8,
  input  in_9,
  input  in_10,
  input  in_11,
  input  in_12,
  input  in_13,
  input  in_14,
  input  in_15,
  input  in_16,
  input  in_17,
  input  in_18,
  input  in_19,
  input  \T_триггер ,
  input  \JK_триггер ,
  input  in_22,
  input  in_23,
  input  in_24,
  input  in_25,
  input  in_26,
  input  in_27,
  input  in_28,
  input  in_29,
  input  in_30,
  input  in_31,
  output out_32,
  output out_33,
  output out_34,
  output out_35,
  output out_36,
  output out_37,
  output out_38,
  output out_39,
  output out_40,
  output out_41,
  output out_42,
  output out_43,
  output [3:0] out_44,
  output out_45,
  output out_46
);

  wire not_1_out, not_2_out, \детектор_переднего_фронта_1_out_2 , \детектор_переднего_фронта_2_out_2 ;

  \SR_триггер  \sr_триггер_1  (.in_1(\SR_триггер ), .in_2(in_4), .in_3(in_7), .out_4(out_32), .out_5(out_35));
  \T_триггер  \t_триггер_1  (.T(in_24), .in_3(in_27), .out_5(out_42), .out_6(out_45), .in_1(\T_триггер ), .in_4(in_30));
  \Детектор_переднего_фронта  \u_детектор_переднего_фронта_1  (
    .in_1(in_16), .out_2(\детектор_переднего_фронта_1_out_2 ));
  \D_триггер  \d_триггер_1  (.in_2(in_5), .in_3(in_8), .out_5(out_33), .out_6(out_36), .in_1(in_2), .in_4(in_10));
  \D_триггер  \d_триггер_2  (
    .in_2(in_14), .in_3(\детектор_переднего_фронта_1_out_2 ), .out_5(out_38), .out_6(out_40), .in_1(in_12),
    .in_4(in_18));
  \JK_триггер  \jk_триггер_1  (
    .in_2(in_23), .in_3(in_26), .in_4(in_28), .out_6(out_43), .out_7(out_46), .in_1(\JK_триггер ),
    .in_5(in_31));
  not not_1 (not_1_out, in_9);
  not not_2 (not_2_out, in_17);
  \Детектор_переднего_фронта  \u_детектор_переднего_фронта_2  (
    .in_1(not_2_out), .out_2(\детектор_переднего_фронта_2_out_2 ));
  \D_триггер  \d_триггер_3  (.in_2(in_6), .in_3(not_1_out), .out_5(out_34), .out_6(out_37), .in_1(in_3), .in_4(in_11));
  \D_триггер  \d_триггер_4  (
    .in_2(in_15), .in_3(\детектор_переднего_фронта_2_out_2 ), .out_5(out_39), .out_6(out_41), .in_1(in_13),
    .in_4(in_19));
  \Бинарный_счётчик  \u_бинарный_счётчик_1  (.in_1(in_22), .in_2(in_25), .in_3(in_29), .out_4(out_44));
  // Probe on out_44

  // Notes on the sheet:
  //   D триггер (верхний уровень)
  //   D триггер (передний фронт)
  //   D триггер (нижний уровень)
  //   D триггер (задний фронт)
  //   Бинарный счётчик
endmodule

module \SR_триггер  (
  input  in_1,
  input  in_2,
  input  in_3,
  output out_4,
  output out_5
);

  wire nand_1_out, nand_2_out;

  nand nand_1 (nand_1_out, in_1, in_2);
  nand nand_2 (nand_2_out, in_2, in_3);
  nand nand_3 (out_4, nand_1_out, out_5);
  nand nand_4 (out_5, out_4, nand_2_out);
endmodule

module \D_триггер  (
  input  in_1,
  input  in_2,
  input  in_3,
  input  in_4,
  output out_5,
  output out_6
);

  wire nand_1_out, nand_2_out;

  nand nand_1 (nand_1_out, in_2, in_3);
  nand nand_2 (nand_2_out, in_3, ~in_2);  // NAND_Gate
  nand nand_3 (out_5, ~in_1, nand_1_out, out_6);  // NAND_Gate
  nand nand_4 (out_6, out_5, nand_2_out, ~in_4);  // NAND_Gate
endmodule

module \Детектор_переднего_фронта  (
  input  in_1,
  output out_2
);

  wire not_1_out, not_2_out, not_3_out;

  not not_1 (not_1_out, not_2_out);
  not not_2 (not_2_out, in_1);
  not not_3 (not_3_out, not_1_out);
  and and_1 (out_2, not_3_out, in_1);
endmodule

module \T_триггер  (
  input  in_1,
  input  T,
  input  in_3,
  input  in_4,
  output out_5,
  output out_6
);

  wire xor_1_out, \детектор_переднего_фронта_1_out_2 ;

  xor xor_1 (xor_1_out, out_5, T);
  \Детектор_переднего_фронта  \u_детектор_переднего_фронта_1  (
    .in_1(in_3), .out_2(\детектор_переднего_фронта_1_out_2 ));
  \D_триггер  \d_триггер_1  (
    .in_2(xor_1_out), .in_3(\детектор_переднего_фронта_1_out_2 ), .out_5(out_5), .out_6(out_6), .in_1(in_1),
    .in_4(in_4));
endmodule

module \JK_триггер  (
  input  in_1,
  input  in_2,
  input  in_3,
  input  in_4,
  input  in_5,
  output out_6,
  output out_7
);

  wire and_1_out, and_2_out, not_1_out, or_1_out, \детектор_переднего_фронта_1_out_2 ;

  not not_1 (not_1_out, in_3);
  and and_1 (and_1_out, out_7, in_2);
  or or_1 (or_1_out, and_1_out, and_2_out);
  and and_2 (and_2_out, not_1_out, out_6);
  \Детектор_переднего_фронта  \u_детектор_переднего_фронта_1  (
    .in_1(in_4), .out_2(\детектор_переднего_фронта_1_out_2 ));
  \D_триггер  \d_триггер_1  (
    .in_2(or_1_out), .in_3(\детектор_переднего_фронта_1_out_2 ), .out_5(out_6), .out_6(out_7), .in_1(in_1),
    .in_4(in_5));
endmodule

module \Бинарный_счётчик  (
  input  in_1,
  input  in_2,
  input  in_3,
  output [3:0] out_4
);

  wire \t_триггер_1_out_6 , \t_триггер_2_out_6 , \t_триггер_3_out_6 ;

  \T_триггер  \t_триггер_1  (
    .T(in_1), .in_3(in_2), .out_5(out_4[0]), .out_6(\t_триггер_1_out_6 ), .in_1(1'b0), .in_4(in_3));
  \T_триггер  \t_триггер_2  (
    .T(in_1), .in_3(\t_триггер_1_out_6 ), .out_5(out_4[1]), .out_6(\t_триггер_2_out_6 ), .in_1(1'b0),
    .in_4(in_3));
  \T_триггер  \t_триггер_3  (
    .T(in_1), .in_3(\t_триггер_2_out_6 ), .out_5(out_4[2]), .out_6(\t_триггер_3_out_6 ), .in_1(1'b0),
    .in_4(in_3));
  \T_триггер  \t_триггер_4  (
    .T(in_1), .in_3(\t_триггер_3_out_6 ), .out_5(out_4[3]), .in_1(1'b0), .in_4(in_3));  // open: out_6
endmodule
